// Logisim project Lab 2 COA.circ as structural Verilog: 1 circuit, main circuit main
module main (
);

  wire and_1_out, and_2_out, and_3_out, and_4_out, and_5_out, and_6_out, and_7_out, and_8_out, and_9_out,
       and_10_out, and_11_out, and_12_out, and_13_out, and_14_out, and_15_out, and_16_out, and_17_out,
       and_18_out, and_19_out, and_20_out, and_21_out, and_22_out, and_23_out, and_24_out, and_25_out,
       and_26_out, and_27_out, and_28_out, clock_1_out, clock_3_out, clock_4_out, clock_5_out, clock_6_out,
       clock_7_out, clock_8_out, not_1_out, not_2_out, not_3_out, not_4_out, not_5_out, not_6_out, not_7_out,
       not_8_out, not_9_out, not_10_out, not_11_out, not_12_out, or_3_out;

  // OR_Gate or_1 is placed but not wired
  not not_1 (not_1_out, 1'b1);
  not not_2 (not_2_out, 1'b1);
  not not_3 (not_3_out, 1'b0);
  and and_1 (and_1_out, 1'b1, 1'b1);
  and and_2 (and_2_out, 1'b1, 1'b0);
  and and_3 (and_3_out, 1'b1, 1'b0);
  Clock clock_1 (.out(clock_1_out));
  and and_4 (and_4_out, not_1_out, not_2_out, 1'b0);
  and and_5 (and_5_out, 1'b1, 1'b1, 1'b0);
  and and_6 (and_6_out, not_1_out, 1'b1, not_3_out);
  and and_7 (and_7_out, not_1_out, not_2_out, not_3_out);
  or or_2 (clock_1_out, and_1_out, and_2_out, and_3_out);
  or or_3 (or_3_out, and_4_out, and_5_out, and_6_out, and_7_out);
  Clock clock_2 (.out(or_3_out));
  not not_4 (not_4_out, 1'b1);
  not not_5 (not_5_out, 1'b1);
  not not_6 (not_6_out, clock_1_out);
  and and_8 (and_8_out, 1'b1, 1'b1);
  and and_9 (and_9_out, 1'b1, clock_1_out);
  and and_10 (and_10_out, 1'b1, clock_1_out);
  Clock clock_3 (.out(clock_3_out));
  and and_11 (and_11_out, not_4_out, not_5_out, clock_1_out);
  and and_12 (and_12_out, 1'b1, 1'b1, clock_1_out);
  and and_13 (and_13_out, not_4_out, 1'b1, not_6_out);
  and and_14 (and_14_out, not_4_out, not_5_out, not_6_out);
  or or_4 (clock_3_out, and_8_out, and_9_out, and_10_out);
  Clock clock_4 (.out(clock_4_out));
  or or_5 (clock_4_out, and_11_out, and_12_out, and_13_out, and_14_out);
  not not_7 (not_7_out, 1'b1);
  not not_8 (not_8_out, 1'b0);
  not not_9 (not_9_out, clock_3_out);
  and and_15 (and_15_out, 1'b1, 1'b0);
  and and_16 (and_16_out, 1'b0, clock_3_out);
  and and_17 (and_17_out, 1'b1, clock_3_out);
  and and_18 (and_18_out, not_7_out, not_8_out, clock_3_out);
  and and_19 (and_19_out, 1'b1, 1'b0, clock_3_out);
  and and_20 (and_20_out, not_7_out, 1'b0, not_9_out);
  and and_21 (and_21_out, not_7_out, not_8_out, not_9_out);
  Clock clock_5 (.out(clock_5_out));
  or or_6 (clock_5_out, and_15_out, and_16_out, and_17_out);
  Clock clock_6 (.out(clock_6_out));
  or or_7 (clock_6_out, and_18_out, and_19_out, and_20_out, and_21_out);
  not not_10 (not_10_out, 1'b1);
  not not_11 (not_11_out, 1'b1);
  not not_12 (not_12_out, clock_5_out);
  and and_22 (and_22_out, 1'b1, 1'b1);
  and and_23 (and_23_out, 1'b1, clock_5_out);
  and and_24 (and_24_out, 1'b1, clock_5_out);
  and and_25 (and_25_out, not_10_out, not_11_out, clock_5_out);
  and and_26 (and_26_out, 1'b1, 1'b1, clock_5_out);
  and and_27 (and_27_out, not_10_out, 1'b1, not_12_out);
  and and_28 (and_28_out, not_10_out, not_11_out, not_12_out);
  Clock clock_7 (.out(clock_7_out));
  or or_8 (clock_7_out, and_22_out, and_23_out, and_24_out);
  Clock clock_8 (.out(clock_8_out));
  or or_9 (clock_8_out, and_25_out, and_26_out, and_27_out, and_28_out);
  DotMatrix #(.matrixrows(1), .dotshape("circle")) dotmatrix_1 (
    .col0(clock_7_out), .col1(clock_8_out), .col2(clock_6_out), .col3(clock_4_out), .col4(or_3_out));
  // NOT_Gate not_13 is placed but not wired
  // AND_Gate and_29 is placed but not wired

  // Notes on the sheet:
  //   A0
  //   B0
  //   C0
  //   A1
  //   B1
  //   C1
  //   A2
  //   B2
  //   C2
  //   A3
  //   B3
  //   C3
endmodule
