// Logisim project lab 1 COA.circ as structural Verilog: 1 circuit, main circuit main
module main (
);

  wire and_1_out, and_2_out, and_3_out, and_4_out, and_5_out, and_6_out, and_7_out, and_8_out,
       decoder_1_out0, decoder_1_out1, decoder_1_out2, decoder_1_out3, decoder_1_out4, decoder_1_out5,
       decoder_1_out6, decoder_1_out7, multiplexer_2_out, multiplexer_3_out, multiplexer_4_out,
       multiplexer_5_out, multiplexer_6_out, multiplexer_7_out, multiplexer_8_out, not_1_out, not_2_out,
       not_3_out, or_1_out, or_2_out, or_3_out, or_4_out, priority_encoder_1_en_out, undriven, undriven_2,
       undriven_3, undriven_4, undriven_5, undriven_6, undriven_7, undriven_8, undriven_9, undriven_10,
       undriven_11, undriven_12, undriven_13, undriven_14, undriven_15, undriven_16, undriven_17, undriven_18;
  wire [2:0] priority_encoder_1_out;
  wire [7:0] multiplexer_1_out;

  Multiplexer #(.select(3), .width(8), .enable("false")) multiplexer_1 (
    .in0({8{1'b0}}), .in1({8{1'b0}}), .in2({8{1'b0}}), .in3({8{1'b0}}), .in4({8{1'b0}}), .in5({8{1'b0}}),
    .in6({8{1'b0}}), .in7(8'h6f), .out(multiplexer_1_out), .sel(3'b111));
  DotMatrix #(.matrixcols(1), .matrixrows(8), .dotshape("circle")) dotmatrix_1 (.col0(multiplexer_1_out));
  or or_1 (or_1_out, 1'b1, 1'b1, 1'b1, 1'b1);
  or or_2 (or_2_out, 1'b1, 1'b1, 1'b1, 1'b1);
  or or_3 (or_3_out, 1'b1, 1'b1, 1'b1, 1'b1);
  Multiplexer #(.enable("false")) multiplexer_2 (.in0(1'b1), .in1(1'b1), .out(multiplexer_2_out), .sel(1'b1));
  Multiplexer #(.enable("false")) multiplexer_3 (.in0(1'b1), .in1(1'b1), .out(multiplexer_3_out), .sel(1'b1));
  Multiplexer #(.enable("false")) multiplexer_4 (.in0(1'b1), .in1(1'b1), .out(multiplexer_4_out), .sel(1'b1));
  Multiplexer #(.enable("false")) multiplexer_5 (.in0(1'b1), .in1(1'b1), .out(multiplexer_5_out), .sel(1'b1));
  DotMatrix #(.matrixcols(1), .matrixrows(1)) dotmatrix_2 (.col0(or_1_out));
  DotMatrix #(.matrixcols(1), .matrixrows(1)) dotmatrix_3 (.col0(or_2_out));
  Multiplexer #(.enable("false")) multiplexer_6 (
    .in0(multiplexer_2_out), .in1(multiplexer_3_out), .out(multiplexer_6_out), .sel(1'b1));
  Multiplexer #(.enable("false")) multiplexer_7 (
    .in0(multiplexer_4_out), .in1(multiplexer_5_out), .out(multiplexer_7_out), .sel(1'b1));
  DotMatrix #(.matrixcols(1), .matrixrows(1)) dotmatrix_4 (.col0(or_3_out));
  DotMatrix #(.matrixcols(1), .matrixrows(1), .dotshape("circle")) dotmatrix_5 (.col0(multiplexer_8_out));
  Multiplexer #(.enable("false")) multiplexer_8 (
    .in0(multiplexer_6_out), .in1(multiplexer_7_out), .out(multiplexer_8_out), .sel(1'b1));
  not not_1 (not_1_out, 1'b1);
  not not_2 (not_2_out, 1'b1);
  DotMatrix #(.matrixcols(1), .matrixrows(1), .dotshape("circle")) dotmatrix_6 (.col0(priority_encoder_1_en_out));
  not not_3 (not_3_out, 1'b1);
  Priority_Encoder priority_encoder_1 (
    .in0(1'b0), .in1(1'b0), .in2(1'b1), .in3(1'b0), .in4(1'b1), .in5(1'b0), .in6(1'b0), .in7(1'b0),
    .out(priority_encoder_1_out), .en_in(1'b1), .en_out(priority_encoder_1_en_out));  // open: gs
  DotMatrix #(.matrixcols(1), .matrixrows(3), .dotshape("circle")) dotmatrix_7 (.col0(priority_encoder_1_out));
  Decoder #(.select(3)) decoder_1 (
    .out0(decoder_1_out0), .out1(decoder_1_out1), .out2(decoder_1_out2), .out3(decoder_1_out3),
    .out4(decoder_1_out4), .out5(decoder_1_out5), .out6(decoder_1_out6), .out7(decoder_1_out7), .sel(3'b010));  // open: en
  and and_1 (and_1_out, not_1_out, not_2_out, not_3_out, 1'b1);
  and and_2 (and_2_out, 1'b1, not_2_out, not_3_out, 1'b1);
  and and_3 (and_3_out, not_3_out, 1'b1, not_1_out, 1'b1);
  and and_4 (and_4_out, undriven, undriven_2, undriven_3, 1'b1);
  and and_5 (and_5_out, undriven_4, undriven_5, undriven_6, 1'b1);
  and and_6 (and_6_out, undriven_7, undriven_8, undriven_9, undriven_10);
  and and_7 (and_7_out, undriven_11, undriven_12, undriven_13, undriven_14);
  and and_8 (and_8_out, undriven_15, undriven_16, undriven_17, undriven_18);
  // AND_Gate and_9 is placed but not wired
  _7_Segment_Display u_7_segment_display_1 (
    .g(decoder_1_out3), .f(decoder_1_out2), .a(decoder_1_out1), .b(decoder_1_out0), .e(decoder_1_out4),
    .d(decoder_1_out5), .c(decoder_1_out6), .dp(decoder_1_out7));
  or or_4 (or_4_out, and_1_out, and_2_out, and_3_out, and_4_out, and_5_out, and_6_out, and_7_out, and_8_out);

  // Notes on the sheet:
  //   D1
  //   D2
  //   D3
  //   D4
  //   D6
  //   D5
  //   D7
  //   S0
  //   S1
  //   S2
endmodule
